# Fritzing sketch WiringDiagram (saved by Fritzing 0.9.3b)

parts:
  Part1 = Arduino Uno (Rev3)
  LED1 = smd LED [color="Yellow (595nm)" package="1206 [SMD]"]
  GY1 = MPU-6050 Board GY-521 [form="♀ (female)" package=THT]
  LED2 = smd LED [color="Yellow (595nm)" package="1206 [SMD]"]
  LED3 = smd LED [color="Yellow (595nm)" package="1206 [SMD]"]
  LED4 = smd LED [color="Yellow (595nm)" package="1206 [SMD]"]
  R2 = Resistor [tolerance=±5% resistance=220 package="2512 [SMD]"]
  R3 = Resistor [tolerance=±5% resistance=220 package="2512 [SMD]"]
  R4 = Resistor [tolerance=±5% resistance=220 package="2512 [SMD]"]
  R5 = Resistor [tolerance=±5% resistance=220 package="2512 [SMD]"]
  S2 = Pushbutton [package="[SMD]"]
  S3 = Pushbutton [package="[SMD]"]
  J1 = Piezo Speaker
  S1 = Pushbutton [package="[THT]"]
  Part2 = Arduino Prototyping Shield
  GY2 = MPU-6050 Board GY-521 [form="♀ (female)" package=THT]
  S4 = Pushbutton [package="[THT]"]
  S5 = Pushbutton [package="[THT]"]
  S6 = Pushbutton [package="[THT]"]
  LED9 = LED - 3mm [color="Yellow (592nm)" package="3 mm [THT]"]
  LED10 = LED - 3mm [color="Yellow (592nm)" package="3 mm [THT]"]  # not connected
  LED11 = LED - 3mm [color="Yellow (592nm)" package="3 mm [THT]"]
  LED12 = LED - 3mm [color="Yellow (592nm)" package="3 mm [THT]"]
  J2 = Piezo Speaker
  R6 = Resistor [tolerance=±5% resistance=680 package=THT]
  R7 = Resistor [tolerance=±5% resistance=680 package=THT]
  Part3 = Arduino Uno (Rev3)  # not connected

nets:
  N1: Part1.GND, GY1.pin2
  N2: Part1.A4/SDA, GY1.pin3
  N3: Part1.A5/SCL, GY1.pin4
  N4: Part1.D4, Part1.D5_PWM, S2.Pin_3, S2.Pin_4, S1.Pin_3, S1.Pin_4
  N5: Part1.D6_PWM, S3.Pin_3, S3.Pin_4
  N6: Part1.D7, J1.pin2
  N7: Part1.5V, GY1.pin1
  N8: LED1.anode, R3.Pin_0
  N9: LED2.anode, R4.Pin_0
  N10: LED3.anode, R2.Pin_0
  N11: LED4.anode, R5.Pin_0
  N12: R2.Pin_1, R5.Pin_1
  N13: R3.Pin_1, R4.Pin_1
  N14: Part2.GND, Part2.N$289, Part2.N$320, Part2.N$358, GY2.pin2, J2.pin1, R6.Pin_0, R7.Pin_1
  N15: Part2.D2, Part2.N$353, Part2.N$425, LED9.anode
  N16: Part2.D3, Part2.N$246, Part2.N$290, LED11.anode, LED12.anode
  N17: Part2.D4, Part2.N$155, Part2.N$191, S6.Pin_1, S6.Pin_2
  N18: Part2.D5, Part2.N$106, Part2.N$143, S5.Pin_1, S5.Pin_2
  N19: Part2.D6, Part2.N$58, Part2.N$94, S4.Pin_1, S4.Pin_2
  N20: Part2.D7, J2.pin2
  N21: Part2.A4, Part2.N$52, GY2.pin3
  N22: Part2.A5, Part2.N$50, GY2.pin4
  N23: Part2.+5V, Part2.N$379, GY2.pin1
  N24: Part2.N$38, GY2.pin5
  N25: Part2.N$62, Part2.N$77, S4.Pin_3, S4.Pin_4
  N26: Part2.N$64, Part2.N$76, Part2.N$88, Part2.N$96, S5.Pin_3, S5.Pin_4, S6.Pin_3, S6.Pin_4
  N27: Part2.N$153, GY2.pin7
  N28: Part2.N$291, Part2.N$314, Part2.N$436, LED11.cathode, LED12.cathode, R7.Pin_0
  N29: Part2.N$326, Part2.N$354, Part2.N$427, LED9.cathode, R6.Pin_1
  N30: Part2.N$395, GY2.pin6
  N31: Part2.N$408, GY2.pin8

custom parts:
  MPU-6050 Board GY-521: Acelerometro y Giroscopio MPU-6050 Board GY-521
